# Fritzing sketch THDweeterSketch (saved by Fritzing 0.9.3b)
breadboards: 1

parts:
  R1 = Resistor [tolerance=±5% resistance=1k package=THT]
  part = Photon
  RHT1 = Humidity and Temperature Sensor RHT03
  S1 = Pushbutton [package="[THT]"]

nets:
  N1: R1.Pin_0, part.D2, RHT1.Data-signal
  3V3: R1.Pin_1, part.3V3, RHT1.Vcc
  N2: part.GND, RHT1.GND_2, S1.Pin_3, S1.Pin_4
  N3: part.D5, S1.Pin_1, S1.Pin_2
